# Fritzing sketch teleinfo_bbb (saved by Fritzing 0.8.5b)
breadboards: 1

parts:
  SFH620A = IC, DIP package, 4 pins [part_number=OPTO]
  R1 = Resistor [tolerance=±5% resistance=3.3k package=THT]
  J1 = Screw terminal - 2 pins [part_number=Téléinfo package=THT]
  R2 = Resistor [tolerance=±5% resistance=220 package=THT]
  BeagleBone1 = BeagleBone Black

nets:
  N1: SFH620A.pin1, R1.Pin_1
  N2: SFH620A.pin2, J1.pin2
  N3: SFH620A.pin3, BeagleBone1.no_name_yet#1
  N4: SFH620A.pin4, R2.Pin_0, BeagleBone1.no_name_yet#26
  N5: R1.Pin_0, J1.pin1
  N6: R2.Pin_1, BeagleBone1.no_name_yet#3

notes:
  I1
  I2

custom parts:
  BeagleBone Black: BeagleBone Black rev. A5B
