# Fritzing sketch esp8266_led (saved by Fritzing 0.9.2b)
breadboards: 1

parts:
  MOD-WIFI-ESP8266-DEV1 = Olimex ESP8266 DEV
  Power_plug1 = Power plug
  R1 = Resistor [tolerance=±5% resistance=220 package=THT]
  LED1 = LED - 5mm [color="Red (633nm)" package="5 mm [THT]"]
  S1 = Pushbutton [package="[THT]"]
  S2 = Pushbutton [package="[THT]"]

nets:
  3.3V: MOD-WIFI-ESP8266-DEV1.3.3V, Power_plug1.VCC
  N1: MOD-WIFI-ESP8266-DEV1.GPIO5, R1.Pin_0
  N2: MOD-WIFI-ESP8266-DEV1.RSTB, S2.Pin_3, S2.Pin_4
  N3: MOD-WIFI-ESP8266-DEV1.GPIO0, S1.Pin_1, S1.Pin_2
  N4: Power_plug1.GND, LED1.cathode, S1.Pin_3, S1.Pin_4
  N5: R1.Pin_1, LED1.anode
  N6: S2.Pin_1, S2.Pin_2

notes:
  3.3V DC
  Pin11 / GPIO5
  Bouton
  Reset
  Bouton
  Flash

custom parts:
  Olimex ESP8266 DEV: MOD-WIFI-ESP8266-DEV is the ultimate development board for ESP8266 with all GPIOs and resources exposed, can be soldered to PCB or used with breadboard and UEXT. Small U.FL connector is provided for external antenna connection. ESP8266 is very highly integrated SOC which includes Xtensa LX106 core processor, RAM, RF front end and allow WIFI TCP-IP stack to be implemented on board with just few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
