# Fritzing sketch teleinfo_rpi (saved by Fritzing 0.8.5b)
breadboards: 1

parts:
  Raspberry_Pi1 = Raspberry Pi (Model B)
  SFH620A = IC, DIP package, 4 pins [part_number=OPTO]
  R1 = Resistor [tolerance=±5% resistance=3.3k package=THT]
  J1 = Screw terminal - 2 pins [part_number=Téléinfo package=THT]
  R2 = Resistor [tolerance=±5% resistance=220 package=THT]

nets:
  N1: Raspberry_Pi1.3V3, R2.Pin_1
  N2: Raspberry_Pi1.GND, SFH620A.pin3
  N3: Raspberry_Pi1.RXD, SFH620A.pin4, R2.Pin_0
  N4: SFH620A.pin1, R1.Pin_1
  N5: SFH620A.pin2, J1.pin2
  N6: R1.Pin_0, J1.pin1

notes:
  I1
  I2

custom parts:
  Raspberry Pi (Model B): Raspberry Pi Single-board Computer, Model B
